# Fritzing sketch Projeto_sismico (saved by Fritzing 0.9.3b)
breadboards: 1

parts:
  ZS-042_RTC1 = ZS-042 RTC Module
  WeMos_D1_Mini_Relay_Shield_V1 = WeMos D1 Mini Relay Shield V2
  Componente1 = Arduino Uno (Rev3)
  LED1 = LEDs [package=led10mm]  # not connected
  U1 = Keyes Tilt Switch [package=THT]

nets:
  N1: ZS-042_RTC1.GND, WeMos_D1_Mini_Relay_Shield_V1.G, U1.ground
  VCC: ZS-042_RTC1.VCC, WeMos_D1_Mini_Relay_Shield_V1.5V, U1.power
  N2: ZS-042_RTC1.SDA, Componente1.A4/SDA
  N3: ZS-042_RTC1.SCL, Componente1.A5/SCL
  N4: WeMos_D1_Mini_Relay_Shield_V1.D1, Componente1.D8
  N5: Componente1.D7, U1.signal

custom parts:
  LEDs: LEDs Standard schematic elements and footprints for 5mm, 3mm, 1206, and 0603 sized LEDs. 5mm - Spark Fun Electronics SKU : COM-00529 (and others)
  Keyes Tilt Switch: Keyes Tilt Switch Sensor Module for Arduino (Works with Official Arduino Boards). Working voltage: 3.3V~5V; digital switch output (0 & 1); High sensitivity.
